# Fritzing sketch back (saved by Fritzing 0.9.3b)

parts:
  DISTANCE = female pin header, 4 pins [form="♀ (female)"]
  ESP32-back = MH-ET Live Minikit for ESP32

nets:
  5V: DISTANCE.pin1, ESP32-back.VCC
  DIST_PIN_TRIGG: DISTANCE.pin2, ESP32-back.IO16
  DIST_PIN_ECHO: DISTANCE.pin3, ESP32-back.IO17
  GND: DISTANCE.pin4, ESP32-back.GND

notes:
  GND
  ECHO
  TRIGGER
  5V

custom parts:
  MH-ET Live Minikit for ESP32: MH-ET Live Minikit for ESP32 ( http://mh.nodebb.com/topic/8/mh-et-live-minikit-for-esp32/2/) PCB footprint is invalid.
