# Fritzing sketch back_v1 (saved by Fritzing 1.0.0rc)
perfboards: 1

parts:
  Part1 = GY-VL53L0XV2 Laser Ranger Module
  A1 = XIAO ESP32C3-tht

nets:
  N1: Part1.VCC, A1.Pin_22
  N2: Part1.GND, A1.Pin_21
  N3: Part1.SCL, A1.Pin_19
  N4: Part1.SDA, A1.Pin_18

custom parts:
  GY-VL53L0XV2 Laser Ranger Module: The GY-VL53L0XV2 is based on the VL53L0X from ST Microelectronics, a time-of-flight ranging system integrated into a compact module.
  XIAO ESP32C3-tht: Seeed Studio XIAO ESP32C3 adopts new RISC-V architecture, supporting both Wi-Fi and BLE wireless connectivities.
